// Logisim project Main.circ as structural Verilog: 7 circuits, main circuit main
module main (
);

  wire clock_1_out, EB, MU, RB, RESET_IP_out, RESET_MD_out, WBR, WMD;
  wire [1:0] MIP, MRD, OPB;
  wire [3:0] OPU;
  wire [7:0] bit_extender_1_out, bit_extender_2_out, IP_4, IP_IMM, IP_q, multiplexer_1_out, multiplexer_2_out;
  wire [23:0] MI_data;
  wire [31:0] bancoreg_1_o1, bancoreg_1_o2, bancoreg_1_od, bancoreg_1_r1, bit_extender_3_out, imm_1_res,
       load_1_res, MD_dout, multiplexer_3_out, multiplexer_4_out, RU;

  Bit_Extender #(.in_width(32), .out_width(8), .\type ("zero")) bit_extender_1 (.in(RU), .out(bit_extender_1_out));
  Multiplexer #(.select(2), .width(8)) multiplexer_1 (
    .in0(IP_4), .in1(IP_IMM), .in2(bit_extender_1_out), .in3(IP_q), .out(multiplexer_1_out), .sel(MIP));
  Clock clock_1 (.out(clock_1_out));
  Register IP (.D(multiplexer_2_out), .en(1'b1), .clk(clock_1_out), .Q(IP_q), .clr(RESET_IP_out));
  Multiplexer #(.width(8)) multiplexer_2 (.in0(multiplexer_1_out), .in1(IP_4), .out(multiplexer_2_out), .sel(RB));
  Button RESET_IP (.out(RESET_IP_out));
  Bit_Extender #(.in_width(32), .out_width(8), .\type ("zero")) bit_extender_2 (
    .in(imm_1_res), .out(bit_extender_2_out));
  Adder adder_1 (.a(8'h1), .b(IP_q), .out(IP_4));  // open: cin, cout
  Adder adder_2 (.a(IP_q), .b(bit_extender_2_out), .out(IP_IMM));  // open: cin, cout
  ROM #(.dataWidth(24)) MI (.addr(IP_q), .data(MI_data));
  Imm imm_1 (.INST(MI_data), .RES(imm_1_res));
  // Probe on bancoreg_1_r1
  BancoReg bancoreg_1 (
    .CLK(clock_1_out), .D(multiplexer_4_out), .RS1(MI_data[12:9]), .RS2(MI_data[16:13]), .RD(MI_data[5:2]),
    .W(WBR), .R1(bancoreg_1_r1), .O1(bancoreg_1_o1), .O2(bancoreg_1_o2), .OD(bancoreg_1_od));
  Multiplexer #(.width(32)) multiplexer_3 (.in0(bancoreg_1_o2), .in1(imm_1_res), .out(multiplexer_3_out), .sel(MU));
  Multiplexer #(.select(2), .width(32)) multiplexer_4 (
    .in0(RU), .in1(MD_dout), .in2(bit_extender_3_out), .in3(load_1_res), .out(multiplexer_4_out), .sel(MRD));
  assign bit_extender_3_out = {{24{1'b0}}, IP_4};  // Bit_Extender bit_extender_3
  UC uc_1 (.INST(MI_data), .WBR(WBR), .MU(MU), .WMD(WMD), .OPU(OPU), .OPB(OPB), .EB(EB), .MIP(MIP), .MRD(MRD));
  Branch branch_1 (.OPR(OPB), .OP1(bancoreg_1_o1), .OP2(bancoreg_1_o2), .EN(EB), .RES(RB));
  ULA ula_1 (.OPR(OPU), .OP1(bancoreg_1_o1), .OP2(multiplexer_3_out), .RES(RU));
  Load load_1 (.IMM(imm_1_res), .BASE(bancoreg_1_od), .RES(load_1_res));
  Button RESET_MD (.out(RESET_MD_out));
  RAM #(.clearpin("true"), .dataWidth(32), .enables("line")) MD (
    .addr(RU[7:0]), .we(WMD), .clk(clock_1_out), .din(bancoreg_1_o2), .dout(MD_dout), .clr(RESET_MD_out));

  // Notes on the sheet:
  //   contents of MI (hex, n*v repeats v):
  //   10e 2005 10a 5 42
endmodule

module BancoReg (
  input  CLK,
  input  [31:0] D,
  input  [3:0] RS1,
  input  [3:0] RS2,
  input  [3:0] RD,
  input  W,
  output [31:0] R1,
  output [31:0] O1,
  output [31:0] O2,
  output [31:0] OD
);

  wire demultiplexer_1_out0, demultiplexer_1_out1, demultiplexer_1_out2, demultiplexer_1_out3,
       demultiplexer_1_out4, demultiplexer_1_out5, demultiplexer_1_out6, demultiplexer_1_out7,
       demultiplexer_1_out8, demultiplexer_1_out9, demultiplexer_1_out10, demultiplexer_1_out11,
       demultiplexer_1_out12, demultiplexer_1_out13, demultiplexer_1_out14, demultiplexer_1_out15;
  wire [31:0] register_1_q, register_3_q, register_4_q, register_5_q, register_6_q, register_7_q,
       register_8_q, register_9_q, register_10_q, register_11_q, register_12_q, register_13_q, register_14_q,
       register_15_q, register_16_q;

  Demultiplexer #(.select(4)) demultiplexer_1 (
    .out0(demultiplexer_1_out0), .out1(demultiplexer_1_out1), .out2(demultiplexer_1_out2),
    .out3(demultiplexer_1_out3), .out4(demultiplexer_1_out4), .out5(demultiplexer_1_out5),
    .out6(demultiplexer_1_out6), .out7(demultiplexer_1_out7), .out8(demultiplexer_1_out8),
    .out9(demultiplexer_1_out9), .out10(demultiplexer_1_out10), .out11(demultiplexer_1_out11),
    .out12(demultiplexer_1_out12), .out13(demultiplexer_1_out13), .out14(demultiplexer_1_out14),
    .out15(demultiplexer_1_out15), .in(W), .sel(RD));
  Register #(.width(32)) register_1 (.D(D), .en(demultiplexer_1_out0), .clk(CLK), .Q(register_1_q), .clr(1'b1));
  Register #(.width(32)) register_2 (.D(D), .en(demultiplexer_1_out1), .clk(CLK), .Q(R1));  // open: clr
  Register #(.width(32)) register_3 (.D(D), .en(demultiplexer_1_out2), .clk(CLK), .Q(register_3_q));  // open: clr
  Register #(.width(32)) register_4 (.D(D), .en(demultiplexer_1_out3), .clk(CLK), .Q(register_4_q));  // open: clr
  Register #(.width(32)) register_5 (.D(D), .en(demultiplexer_1_out4), .clk(CLK), .Q(register_5_q));  // open: clr
  Register #(.width(32)) register_6 (.D(D), .en(demultiplexer_1_out5), .clk(CLK), .Q(register_6_q));  // open: clr
  Register #(.width(32)) register_7 (.D(D), .en(demultiplexer_1_out6), .clk(CLK), .Q(register_7_q));  // open: clr
  Register #(.width(32)) register_8 (.D(D), .en(demultiplexer_1_out7), .clk(CLK), .Q(register_8_q));  // open: clr
  Register #(.width(32)) register_9 (.D(D), .en(demultiplexer_1_out8), .clk(CLK), .Q(register_9_q));  // open: clr
  Register #(.width(32)) register_10 (.D(D), .en(demultiplexer_1_out9), .clk(CLK), .Q(register_10_q));  // open: clr
  Register #(.width(32)) register_11 (.D(D), .en(demultiplexer_1_out10), .clk(CLK), .Q(register_11_q));  // open: clr
  Register #(.width(32)) register_12 (.D(D), .en(demultiplexer_1_out11), .clk(CLK), .Q(register_12_q));  // open: clr
  Register #(.width(32)) register_13 (.D(D), .en(demultiplexer_1_out12), .clk(CLK), .Q(register_13_q));  // open: clr
  Register #(.width(32)) register_14 (.D(D), .en(demultiplexer_1_out13), .clk(CLK), .Q(register_14_q));  // open: clr
  Register #(.width(32)) register_15 (.D(D), .en(demultiplexer_1_out14), .clk(CLK), .Q(register_15_q));  // open: clr
  Register #(.width(32)) register_16 (.D(D), .en(demultiplexer_1_out15), .clk(CLK), .Q(register_16_q));  // open: clr
  Multiplexer #(.select(4), .width(32)) multiplexer_1 (
    .in0(register_1_q), .in1(R1), .in2(register_3_q), .in3(register_4_q), .in4(register_5_q),
    .in5(register_6_q), .in6(register_7_q), .in7(register_8_q), .in8(register_9_q), .in9(register_10_q),
    .in10(register_11_q), .in11(register_12_q), .in12(register_13_q), .in13(register_14_q),
    .in14(register_15_q), .in15(register_16_q), .out(O1), .sel(RS1));
  Multiplexer #(.select(4), .width(32)) multiplexer_2 (
    .in0(register_1_q), .in1(R1), .in2(register_3_q), .in3(register_4_q), .in4(register_5_q),
    .in5(register_6_q), .in6(register_7_q), .in7(register_8_q), .in8(register_9_q), .in9(register_10_q),
    .in10(register_11_q), .in11(register_12_q), .in12(register_13_q), .in13(register_14_q),
    .in14(register_15_q), .in15(register_16_q), .out(O2), .sel(RS2));
  Multiplexer #(.select(4), .width(32)) multiplexer_3 (
    .in0(register_1_q), .in1(R1), .in2(register_3_q), .in3(register_4_q), .in4(register_5_q),
    .in5(register_6_q), .in6(register_7_q), .in7(register_8_q), .in8(register_9_q), .in9(register_10_q),
    .in10(register_11_q), .in11(register_12_q), .in12(register_13_q), .in13(register_14_q),
    .in14(register_15_q), .in15(register_16_q), .out(OD), .sel(RD));
endmodule

module ULA (
  input  [3:0] OPR,
  input  [31:0] OP1,
  input  [31:0] OP2,
  output [31:0] RES
);

  wire [31:0] ADD, ANDx, DIV, MODx, MUL, ORx, SLLx, SUB, XORx;

  Adder #(.width(32)) adder_1 (.a(OP1), .b(OP2), .out(ADD));  // open: cin, cout
  Subtractor #(.width(32)) subtractor_1 (.a(OP1), .b(OP2), .out(SUB));  // open: bin, bout
  Divider #(.mode("twosComplement"), .width(32)) divider_1 (.a(OP1), .b(OP2), .out(DIV), .rem(MODx));  // open: upper
  Multiplier #(.mode("twosComplement"), .width(32)) multiplier_1 (.a(OP1), .b(OP2), .out(MUL));  // open: cin, cout
  assign ANDx = OP1 & OP2;  // AND_Gate and_1, 32 bits wide
  assign ORx = OP1 | OP2;  // OR_Gate or_1, 32 bits wide
  assign XORx = OP1 ^ OP2;  // XOR_Gate xor_1, 32 bits wide
  Shifter #(.width(32)) shifter_1 (.in(OP1), .\dist (OP2[4:0]), .out(SLLx));
  Multiplexer #(.select(4), .width(32)) multiplexer_1 (
    .in0(ADD), .in1(SUB), .in2(MUL), .in3(DIV), .in4(MODx), .in5(ANDx), .in6(ORx), .in7(XORx), .in8(ADD),
    .in9(ADD), .in10(ADD), .in11(SLLx), .in12(MODx), .in13(ANDx), .in14(ORx), .in15(XORx), .out(RES),
    .sel(OPR));
endmodule

module Branch (
  input  [1:0] OPR,
  input  [31:0] OP1,
  input  [31:0] OP2,
  input  EN,
  output RES
);

  wire comparator_1_eq, comparator_1_gt, comparator_1_lt, multiplexer_1_out, not_1_out, not_2_out, or_1_out;

  Comparator #(.width(32)) comparator_1 (
    .a(OP1), .b(OP2), .gt(comparator_1_gt), .eq(comparator_1_eq), .lt(comparator_1_lt));
  or or_1 (or_1_out, comparator_1_eq, comparator_1_gt);
  not not_1 (not_1_out, comparator_1_eq);
  Multiplexer #(.select(2)) multiplexer_1 (
    .in0(comparator_1_eq), .in1(not_1_out), .in2(or_1_out), .in3(comparator_1_lt), .out(multiplexer_1_out),
    .sel(OPR));
  not not_2 (not_2_out, multiplexer_1_out);
  and and_1 (RES, not_2_out, EN);
endmodule

module Imm (
  input  [23:0] INST,
  output [31:0] RES
);

  Multiplexer #(.select(2), .width(32)) multiplexer_1 (
    .in1({{22{INST[23]}}, INST[22:13]}), .in2({{22{INST[23]}}, INST[22:17], INST[5:2]}),
    .in3({{17{INST[23]}}, INST[22:8]}), .out(RES), .sel(INST[1:0]));  // open: in0
endmodule

module UC (
  input  [23:0] INST,
  output WBR,
  output MU,
  output WMD,
  output [3:0] OPU,
  output [1:0] OPB,
  output EB,
  output [1:0] MIP,
  output [1:0] MRD
);

  wire and_1_out, and_2_out, and_3_out, nor_1_out, nor_2_out, or_1_out, or_2_out, or_3_out, or_4_out;

  and and_1 (and_1_out, INST[6], ~INST[7]);  // AND_Gate
  and and_2 (and_2_out, INST[0], ~INST[1], ~INST[6], INST[7]);  // AND_Gate
  and and_3 (and_3_out, ~INST[0], INST[1], INST[6], ~INST[7]);  // AND_Gate
  nor nor_1 (nor_1_out, ~INST[6], INST[7], INST[8]);  // NOR_Gate
  nor nor_2 (nor_2_out, INST[6], ~INST[7], INST[8]);  // NOR_Gate
  or or_1 (or_1_out, and_1_out, INST[8]);
  and and_4 (MIP[0], or_1_out, ~INST[0], INST[1]);  // AND_Gate
  or or_2 (or_2_out, and_2_out, and_3_out);
  and and_5 (MIP[1], or_2_out, ~INST[8]);  // AND_Gate
  or or_3 (or_3_out, nor_1_out, INST[1]);
  and and_6 (MRD[0], or_3_out, INST[0]);
  or or_4 (or_4_out, nor_2_out, INST[1]);
  and and_7 (MRD[1], or_4_out, INST[0]);
  or or_5 (WBR, INST[0], ~INST[1]);  // OR_Gate
  or or_6 (MU, INST[0], INST[1]);
  nor nor_3 (WMD, INST[0], ~INST[1], INST[6], INST[7], INST[8]);  // NOR_Gate
  and and_8 (EB, ~INST[0], INST[1], INST[8]);  // AND_Gate

  assign OPB = INST[7:6];
  assign OPU = {INST[0], INST[8:6]};
endmodule

module Load (
  input  [31:0] IMM,
  input  [31:0] BASE,
  output [31:0] RES
);


  assign RES = {BASE[31:16], IMM[15:0]};
endmodule
